// Logisim project DataPath.circ as structural Verilog: 3 circuits, main circuit main
module main (
  input  PC_i,
  input  PC_o,
  input  PC_Sel,
  input  IR_i,
  input  MAR_i,
  input  MDR_i,
  input  MDR_o,
  input  MDR_Sel,
  input  MemRead,
  input  MemWrite,
  input  ACC_i,
  input  ACC_o,
  input  ALU_Sel,
  input  ACC_Sel,
  input  SP_i,
  input  SP_o,
  input  R_i,
  input  R_o,
  output [7:0] IR_to_CU,
  output ZF_to_CU
);

  wire clk_out;
  wire [7:0] ACC_q, ALU_result, controlled_buffer_1_out, MAR_q, MDR_q, Mem2Reg, multiplexer_1_out,
       multiplexer_2_out, multiplexer_3_out, PC_1, PC_q, R_q, SP_q;

  Clock #(.highDuration(1), .lowDuration(1)) clk (.out(clk_out));
  ALU ALU (.SrcA(ACC_q), .SrcB(controlled_buffer_1_out), .ALUSel(ALU_Sel), .Result(ALU_result));
  Multiplexer #(.select(1), .width(8), .disabled("Z"), .enable("false")) multiplexer_1 (
    .in0(controlled_buffer_1_out), .in1(PC_1), .out(multiplexer_1_out), .sel(PC_Sel));
  Multiplexer #(.select(1), .width(8), .disabled("Z"), .enable("false")) multiplexer_2 (
    .in0(controlled_buffer_1_out), .in1(Mem2Reg), .out(multiplexer_2_out), .sel(MDR_Sel));
  Register #(.width(8), .trigger("rising"), .Select("low")) PC (
    .D(multiplexer_1_out), .en(PC_i), .Q(PC_q), .clk(clk_out));  // open: clr
  Register #(.width(8), .trigger("rising"), .Select("low")) IR (
    .D(controlled_buffer_1_out), .en(IR_i), .Q(IR_to_CU), .clk(clk_out));  // open: clr
  Register #(.width(8), .trigger("rising"), .Select("low")) MAR (
    .D(controlled_buffer_1_out), .en(MAR_i), .Q(MAR_q), .clk(clk_out));  // open: clr
  Register #(.width(8), .trigger("rising"), .Select("low")) MDR (
    .D(multiplexer_2_out), .en(MDR_i), .Q(MDR_q), .clk(clk_out));  // open: clr
  Multiplexer #(.select(1), .width(8), .disabled("Z"), .enable("false")) multiplexer_3 (
    .in0(controlled_buffer_1_out), .in1(ALU_result), .out(multiplexer_3_out), .sel(ACC_Sel));
  Register #(.width(8), .trigger("rising"), .Select("low")) ACC (
    .D(multiplexer_3_out), .en(ACC_i), .Q(ACC_q), .clk(clk_out));  // open: clr
  Register #(.width(8), .trigger("rising"), .Select("low")) SP (
    .D(controlled_buffer_1_out), .en(SP_i), .Q(SP_q), .clk(clk_out));  // open: clr
  Register #(.width(8), .trigger("rising"), .Select("low")) R (
    .D(controlled_buffer_1_out), .en(R_i), .Q(R_q), .clk(clk_out));  // open: clr
  // Probe on controlled_buffer_1_out
  assign controlled_buffer_1_out = PC_o ? PC_q : 8'bz;  // Controlled_Buffer controlled_buffer_1
  assign controlled_buffer_1_out = MDR_o ? MDR_q : 8'bz;  // Controlled_Buffer controlled_buffer_2
  assign controlled_buffer_1_out = ACC_o ? ACC_q : 8'bz;  // Controlled_Buffer controlled_buffer_3
  assign controlled_buffer_1_out = SP_o ? SP_q : 8'bz;  // Controlled_Buffer controlled_buffer_4
  assign controlled_buffer_1_out = R_o ? R_q : 8'bz;  // Controlled_Buffer controlled_buffer_5
  Adder #(.width(8)) adder_1 (.a(PC_q), .b(8'h1), .out(PC_1));  // open: cin, cout
  MEM mem_1 (.addr(MAR_q), .din(MDR_q), .wreq(MemWrite), .rreq(MemRead), .clk(clk_out), .dout(Mem2Reg));
  Comparator #(.width(8), .mode("twosComplement")) comparator_1 (
    .a(ACC_q), .b({8{1'b0}}), .eq(ZF_to_CU));  // open: gt, lt
endmodule

module ALU (
  input  [7:0] SrcA,
  input  [7:0] SrcB,
  input  ALUSel,
  output [7:0] Result
);

  wire [7:0] adder_1_out, and_1_out;

  assign and_1_out = SrcA & SrcB;  // AND_Gate and_1, 8 bits wide
  Adder #(.width(8)) adder_1 (.a(SrcA), .b(SrcB), .out(adder_1_out));  // open: cin, cout
  Multiplexer #(.select(1), .width(8), .disabled("Z"), .enable("false")) multiplexer_1 (
    .in0(and_1_out), .in1(adder_1_out), .out(Result), .sel(ALUSel));
endmodule

module MEM (
  input  [7:0] addr,
  input  [7:0] din,
  input  wreq,
  input  rreq,
  input  clk,
  output [7:0] dout
);

  wire register_1_q, register_2_q;
  wire [7:0] ram_1_data;

  Register #(.width(1), .trigger("rising"), .Select("low")) register_1 (
    .D(wreq), .Q(register_1_q), .clk(clk));  // open: en, clr
  Register #(.width(1), .trigger("rising"), .Select("low")) register_2 (
    .D(rreq), .Q(register_2_q), .clk(clk));  // open: en, clr
  RAM #(.addrWidth(8), .dataWidth(8), .bus("separate"), .Select("high")) ram_1 (
    .addr(addr), .din(din), .data(ram_1_data), .str(register_1_q), .sel(1'b1), .clk(clk), .ld(1'b1),
    .clr(1'b0));
  assign dout = register_2_q ? ram_1_data : 8'bz;  // Controlled_Buffer controlled_buffer_1
endmodule
